# Fritzing sketch box_circuit (saved by Fritzing 0.9.3b)
breadboards: 1

parts:
  Raspberry_Pi1 = Raspberry Pi 2
  J1 = Power Jack [package=power_jack_pth]
  LED1 = LEDs [package=fkit-led-1206]
  Q1 = Basic FET N-Channel [package="TO220 [THT]"]
  LED2 = LEDs [package=fkit-led-1206]
  S1 = Toggle Switch [package=THT]
  Q2 = Basic FET N-Channel [package="TO220 [THT]"]
  S2 = Pushbutton [package="[THT]"]
  J2 = Peltier Element
  IC1 = L293D [package=THT]
  U1 = 74HC04_HEX_INVERTER [package=dil14]

nets:
  GND: Raspberry_Pi1.GND, J1.GND, Q1.source, Q2.source, S2.Pin_4, IC1.0V, U1.GND
  N1: Raspberry_Pi1.GPIO8, IC1.In_3, U1.4A
  N2: Raspberry_Pi1.GPIO25, IC1.Enable_2
  N3: Raspberry_Pi1.GPIO23, Q2.gate
  N4: Raspberry_Pi1.GPIO18, Q1.gate
  5V: Raspberry_Pi1.5V, IC1.+V, U1.VCC
  N5: J1.PWR, S1.COM
  N6: LED1.A, LED2.A, S1.L1, S2.Pin_2, IC1.+Vmotor
  N7: LED1.C, Q1.drain
  N8: LED2.C, Q2.drain
  N9: J2.pin1, IC1.Out_4_(_Controlled_by_Enable_2_)
  N10: J2.pin2, IC1.Out_3_(_Controlled_by_Enable_2_)
  N11: IC1.In_4, U1.4Y

notes:
  Panel-mount jack/switch:
  DC 12V 1A
  (switch optional)
  Visible LED Strip
  IR LED Strip
  Stand-in for 12V-5V step-down to USB for RPi (AMZN "12V micro-usb" ~$10)
  Tank electrodes
