# Fritzing sketch fishbox_circuit (saved by Fritzing 0.9.2b)
breadboards: 1

parts:
  Raspberry_Pi1 = Raspberry Pi 2
  J1 = Power Jack [package=power_jack_pth]
  LED1 = LEDs [package=fkit-led-1206]
  Q1 = Basic FET N-Channel [package="TO220 [THT]"]
  LED2 = LEDs [package=fkit-led-1206]
  S1 = Toggle Switch [package=THT]
  Q2 = Basic FET N-Channel [package="TO220 [THT]"]
  S2 = Pushbutton [package="[THT]"]

nets:
  GND: Raspberry_Pi1.GND, J1.GND, Q1.source, Q2.source, S2.Pin_4
  N1: Raspberry_Pi1.GPIO23, Q2.gate
  N2: Raspberry_Pi1.GPIO18, Q1.gate
  N3: J1.PWR, S1.COM
  N4: LED1.A, LED2.A, S1.L1, S2.Pin_2
  N5: LED1.C, Q1.drain
  N6: LED2.C, Q2.drain

notes:
  Panel-mount jack/switch:
  DC 12V 1A
  (switch optional)
  Visible LED Strip
  IR LED Strip
  Stand-in for 12V-5V step-down to USB for RPi (AMZN "12V micro-usb" ~$10)
